# Fritzing sketch Sleep_coach_tiny_schematic (saved by Fritzing 0.7.12b)
breadboards: 1

parts:
  XTAL2 = Crystal [frequency="16 Mhz" package=THT]
  C6 = Ceramic Capacitor [capacitance=100nF package="100 mil [THT, multilayer]"]
  C7 = Ceramic Capacitor [capacitance=100nF package="100 mil [THT, multilayer]"]
  C9 = Electrolytic Capacitor [capacitance=10µF package="100 mil [THT, electrolytic]"]
  Power_plug2 = Power plug
  U3 = atmega328 [package=dip]
  LED1 = LED - 5mm [color="Blue (525nm)" package="5 mm [THT]"]
  LED2 = LED - 5mm [color="Blue (525nm)" package="5 mm [THT]"]
  LED3 = LED - 5mm [color="Blue (525nm)" package="5 mm [THT]"]
  LED4 = LED - 5mm [color="Blue (525nm)" package="5 mm [THT]"]
  S1 = Pushbutton [package="[THT]"]
  R1 = Resistor [tolerance=±5% resistance=220 package=THT]
  R2 = Resistor [tolerance=±5% resistance=220 package=THT]
  R3 = Resistor [tolerance=±5% resistance=220 package=THT]
  R4 = Resistor [tolerance=±5% resistance=220 package=THT]
  R5 = Resistor [tolerance=±5% resistance=220 package=THT]
  J1 = female pin header, 1 pin [form="♀ (female)"]
  J2 = female pin header, 1 pin [form="♀ (female)"]
  J3 = female pin header, 1 pin [form="♀ (female)"]

nets:
  N1: XTAL2.pin_0, C7.1, U3.XLAT1
  N2: XTAL2.pin_1, C6.1, U3.XLAT2
  GND: C6.0, C7.0, C9.-, Power_plug2.GND, U3.GND, R1.Pin_0, R2.Pin_1, R3.Pin_1, J1.pin1, J2.pin1
  VCC: C9.+, Power_plug2.VCC, U3.VCC, U3.AVCC, U3.AREF, S1.Pin_1, S1.Pin_2
  N3: U3.D5_(PWM), R5.Pin_1
  N4: U3.D6_(PWM), R4.Pin_1
  N5: U3.D9_(PWM), LED3.anode
  N6: U3.D10_(PWM), LED4.anode
  N7: U3.D11_(PWM), S1.Pin_3, S1.Pin_4, R1.Pin_1
  N8: U3.A5, J3.pin1
  N9: LED1.cathode, LED2.cathode
  N10: LED1.anode, R5.Pin_0
  N11: LED2.anode, R4.Pin_0
  N12: LED3.cathode, R2.Pin_0
  N13: LED4.cathode, R3.Pin_0
