# Fritzing sketch Sleep_coach_tiny_schematic_4_up_battery (saved by Fritzing 0.7.12b)
breadboards: 1

parts:
  C15 = Electrolytic Capacitor [capacitance=10µF package="100 mil [THT, electrolytic]"]
  C16 = Electrolytic Capacitor [capacitance=10µF package="100 mil [THT, electrolytic]"]
  LED21 = LED - 5mm [color="Blue (525nm)" package="5 mm [THT]"]
  LED24 = LED - 5mm [color="Blue (525nm)" package="5 mm [THT]"]
  LED25 = LED - 5mm [color="Blue (525nm)" package="5 mm [THT]"]
  LED27 = LED - 5mm [color="Blue (525nm)" package="5 mm [THT]"]
  LED30 = LED - 5mm [color="Blue (525nm)" package="5 mm [THT]"]
  LED31 = LED - 5mm [color="Blue (525nm)" package="5 mm [THT]"]
  LED34 = LED - 5mm [color="Blue (525nm)" package="5 mm [THT]"]
  LED35 = LED - 5mm [color="Blue (525nm)" package="5 mm [THT]"]
  S6 = Pushbutton [package="[THT]"]
  S9 = Pushbutton [package="[THT]"]
  J16 = female pin header, 1 pin [form="♀ (female)"]
  J18 = female pin header, 1 pin [form="♀ (female)"]
  J22 = female pin header, 1 pin [form="♀ (female)"]
  J23 = female pin header, 1 pin [form="♀ (female)"]
  J26 = female pin header, 1 pin [form="♀ (female)"]
  J27 = female pin header, 1 pin [form="♀ (female)"]
  R11 = Resistor [tolerance=±5% resistance=220 package=THT]
  R14 = Resistor [tolerance=±5% resistance=220 package=THT]
  U8 = attiny85 [package=dip]
  U9 = attiny85 [package=dip]
  VCC8 = Battery
  VCC9 = Battery
  C21 = Electrolytic Capacitor [capacitance=10µF package="100 mil [THT, electrolytic]"]
  C22 = Electrolytic Capacitor [capacitance=10µF package="100 mil [THT, electrolytic]"]
  LED52 = LED - 5mm [color="Blue (525nm)" package="5 mm [THT]"]
  LED53 = LED - 5mm [color="Blue (525nm)" package="5 mm [THT]"]
  LED54 = LED - 5mm [color="Blue (525nm)" package="5 mm [THT]"]
  LED55 = LED - 5mm [color="Blue (525nm)" package="5 mm [THT]"]
  LED56 = LED - 5mm [color="Blue (525nm)" package="5 mm [THT]"]
  LED57 = LED - 5mm [color="Blue (525nm)" package="5 mm [THT]"]
  LED58 = LED - 5mm [color="Blue (525nm)" package="5 mm [THT]"]
  LED59 = LED - 5mm [color="Blue (525nm)" package="5 mm [THT]"]
  S14 = Pushbutton [package="[THT]"]
  S15 = Pushbutton [package="[THT]"]
  J40 = female pin header, 1 pin [form="♀ (female)"]
  J41 = female pin header, 1 pin [form="♀ (female)"]
  J42 = female pin header, 1 pin [form="♀ (female)"]
  J43 = female pin header, 1 pin [form="♀ (female)"]
  J44 = female pin header, 1 pin [form="♀ (female)"]
  J45 = female pin header, 1 pin [form="♀ (female)"]
  R19 = Resistor [tolerance=±5% resistance=220 package=THT]
  R20 = Resistor [tolerance=±5% resistance=220 package=THT]
  U14 = attiny85 [package=dip]
  U15 = attiny85 [package=dip]
  VCC14 = Battery
  VCC15 = Battery

nets:
  N1: C15.-, LED21.cathode, LED27.cathode, LED31.cathode, LED34.cathode, J27.pin1, R11.Pin_0, U9.Pin_4, VCC8.-
  N2: C15.+, S6.Pin_3, S6.Pin_4, J22.pin1, U9.Pin_8, VCC8.+
  N3: C16.-, LED24.cathode, LED25.cathode, LED30.cathode, LED35.cathode, J26.pin1, R14.Pin_0, U8.Pin_4, VCC9.-
  N4: C16.+, S9.Pin_3, S9.Pin_4, J23.pin1, U8.Pin_8, VCC9.+
  N5: LED21.anode, LED27.anode, LED31.anode, LED34.anode, U9.Pin_5
  N6: LED24.anode, LED25.anode, LED30.anode, LED35.anode, U8.Pin_5
  N7: S6.Pin_1, S6.Pin_2, R11.Pin_1, U9.Pin_6
  N8: S9.Pin_1, S9.Pin_2, R14.Pin_1, U8.Pin_6
  N9: J16.pin1, U9.Pin_2
  N10: J18.pin1, U8.Pin_2
  N11: C21.-, LED52.cathode, LED55.cathode, LED57.cathode, LED58.cathode, J45.pin1, R19.Pin_0, U15.Pin_4, VCC14.-
  N12: C21.+, S14.Pin_3, S14.Pin_4, J42.pin1, U15.Pin_8, VCC14.+
  N13: C22.-, LED53.cathode, LED54.cathode, LED56.cathode, LED59.cathode, J44.pin1, R20.Pin_0, U14.Pin_4, VCC15.-
  N14: C22.+, S15.Pin_3, S15.Pin_4, J43.pin1, U14.Pin_8, VCC15.+
  N15: LED52.anode, LED55.anode, LED57.anode, LED58.anode, U15.Pin_5
  N16: LED53.anode, LED54.anode, LED56.anode, LED59.anode, U14.Pin_5
  N17: S14.Pin_1, S14.Pin_2, R19.Pin_1, U15.Pin_6
  N18: S15.Pin_1, S15.Pin_2, R20.Pin_1, U14.Pin_6
  N19: J40.pin1, U15.Pin_2
  N20: J41.pin1, U14.Pin_2
