# Fritzing sketch Sleep_coach_tiny_schematic_8_up_battery (saved by Fritzing 0.7.12b)
breadboards: 1

parts:
  C10 = Electrolytic Capacitor [capacitance=10µF package="100 mil [THT, electrolytic]"]
  LED5 = LED - 5mm [color="Blue (525nm)" package="5 mm [THT]"]
  LED6 = LED - 5mm [color="Blue (525nm)" package="5 mm [THT]"]
  LED7 = LED - 5mm [color="Blue (525nm)" package="5 mm [THT]"]
  LED8 = LED - 5mm [color="Blue (525nm)" package="5 mm [THT]"]
  S2 = Pushbutton [package="[THT]"]
  J4 = female pin header, 1 pin [form="♀ (female)"]
  J5 = female pin header, 1 pin [form="♀ (female)"]
  J6 = female pin header, 1 pin [form="♀ (female)"]
  R7 = Resistor [tolerance=±5% resistance=220 package=THT]
  U2 = attiny85 [package=dip]
  VCC2 = Battery
  C11 = Electrolytic Capacitor [capacitance=10µF package="100 mil [THT, electrolytic]"]
  LED9 = LED - 5mm [color="Blue (525nm)" package="5 mm [THT]"]
  LED10 = LED - 5mm [color="Blue (525nm)" package="5 mm [THT]"]
  LED11 = LED - 5mm [color="Blue (525nm)" package="5 mm [THT]"]
  LED12 = LED - 5mm [color="Blue (525nm)" package="5 mm [THT]"]
  S3 = Pushbutton [package="[THT]"]
  J7 = female pin header, 1 pin [form="♀ (female)"]
  J8 = female pin header, 1 pin [form="♀ (female)"]
  J9 = female pin header, 1 pin [form="♀ (female)"]
  R8 = Resistor [tolerance=±5% resistance=220 package=THT]
  U3 = attiny85 [package=dip]
  VCC3 = Battery
  C15 = Electrolytic Capacitor [capacitance=10µF package="100 mil [THT, electrolytic]"]
  C16 = Electrolytic Capacitor [capacitance=10µF package="100 mil [THT, electrolytic]"]
  LED21 = LED - 5mm [color="Blue (525nm)" package="5 mm [THT]"]
  LED24 = LED - 5mm [color="Blue (525nm)" package="5 mm [THT]"]
  LED25 = LED - 5mm [color="Blue (525nm)" package="5 mm [THT]"]
  LED27 = LED - 5mm [color="Blue (525nm)" package="5 mm [THT]"]
  LED30 = LED - 5mm [color="Blue (525nm)" package="5 mm [THT]"]
  LED31 = LED - 5mm [color="Blue (525nm)" package="5 mm [THT]"]
  LED34 = LED - 5mm [color="Blue (525nm)" package="5 mm [THT]"]
  LED35 = LED - 5mm [color="Blue (525nm)" package="5 mm [THT]"]
  S6 = Pushbutton [package="[THT]"]
  S9 = Pushbutton [package="[THT]"]
  J16 = female pin header, 1 pin [form="♀ (female)"]
  J18 = female pin header, 1 pin [form="♀ (female)"]
  J22 = female pin header, 1 pin [form="♀ (female)"]
  J23 = female pin header, 1 pin [form="♀ (female)"]
  J26 = female pin header, 1 pin [form="♀ (female)"]
  J27 = female pin header, 1 pin [form="♀ (female)"]
  R11 = Resistor [tolerance=±5% resistance=220 package=THT]
  R14 = Resistor [tolerance=±5% resistance=220 package=THT]
  U8 = attiny85 [package=dip]
  U9 = attiny85 [package=dip]
  VCC8 = Battery
  VCC9 = Battery
  C19 = Electrolytic Capacitor [capacitance=10µF package="100 mil [THT, electrolytic]"]
  C20 = Electrolytic Capacitor [capacitance=10µF package="100 mil [THT, electrolytic]"]
  LED44 = LED - 5mm [color="Blue (525nm)" package="5 mm [THT]"]
  LED45 = LED - 5mm [color="Blue (525nm)" package="5 mm [THT]"]
  LED46 = LED - 5mm [color="Blue (525nm)" package="5 mm [THT]"]
  LED47 = LED - 5mm [color="Blue (525nm)" package="5 mm [THT]"]
  LED48 = LED - 5mm [color="Blue (525nm)" package="5 mm [THT]"]
  LED49 = LED - 5mm [color="Blue (525nm)" package="5 mm [THT]"]
  LED50 = LED - 5mm [color="Blue (525nm)" package="5 mm [THT]"]
  LED51 = LED - 5mm [color="Blue (525nm)" package="5 mm [THT]"]
  S12 = Pushbutton [package="[THT]"]
  S13 = Pushbutton [package="[THT]"]
  J34 = female pin header, 1 pin [form="♀ (female)"]
  J35 = female pin header, 1 pin [form="♀ (female)"]
  J36 = female pin header, 1 pin [form="♀ (female)"]
  J37 = female pin header, 1 pin [form="♀ (female)"]
  J38 = female pin header, 1 pin [form="♀ (female)"]
  J39 = female pin header, 1 pin [form="♀ (female)"]
  R17 = Resistor [tolerance=±5% resistance=220 package=THT]
  R18 = Resistor [tolerance=±5% resistance=220 package=THT]
  U12 = attiny85 [package=dip]
  U13 = attiny85 [package=dip]
  VCC12 = Battery
  VCC13 = Battery
  C21 = Electrolytic Capacitor [capacitance=10µF package="100 mil [THT, electrolytic]"]
  C22 = Electrolytic Capacitor [capacitance=10µF package="100 mil [THT, electrolytic]"]
  LED52 = LED - 5mm [color="Blue (525nm)" package="5 mm [THT]"]
  LED53 = LED - 5mm [color="Blue (525nm)" package="5 mm [THT]"]
  LED54 = LED - 5mm [color="Blue (525nm)" package="5 mm [THT]"]
  LED55 = LED - 5mm [color="Blue (525nm)" package="5 mm [THT]"]
  LED56 = LED - 5mm [color="Blue (525nm)" package="5 mm [THT]"]
  LED57 = LED - 5mm [color="Blue (525nm)" package="5 mm [THT]"]
  LED58 = LED - 5mm [color="Blue (525nm)" package="5 mm [THT]"]
  LED59 = LED - 5mm [color="Blue (525nm)" package="5 mm [THT]"]
  S14 = Pushbutton [package="[THT]"]
  S15 = Pushbutton [package="[THT]"]
  J40 = female pin header, 1 pin [form="♀ (female)"]
  J41 = female pin header, 1 pin [form="♀ (female)"]
  J42 = female pin header, 1 pin [form="♀ (female)"]
  J43 = female pin header, 1 pin [form="♀ (female)"]
  J44 = female pin header, 1 pin [form="♀ (female)"]
  J45 = female pin header, 1 pin [form="♀ (female)"]
  R19 = Resistor [tolerance=±5% resistance=220 package=THT]
  R20 = Resistor [tolerance=±5% resistance=220 package=THT]
  U14 = attiny85 [package=dip]
  U15 = attiny85 [package=dip]
  VCC14 = Battery
  VCC15 = Battery

nets:
  N1: C10.-, LED5.cathode, LED6.cathode, LED7.cathode, LED8.cathode, J6.pin1, R7.Pin_0, U2.Pin_4, VCC2.-
  N2: C10.+, S2.Pin_3, S2.Pin_4, J5.pin1, U2.Pin_8, VCC2.+
  N3: LED5.anode, LED6.anode, LED7.anode, LED8.anode, U2.Pin_5
  N4: S2.Pin_1, S2.Pin_2, R7.Pin_1, U2.Pin_6
  N5: J4.pin1, U2.Pin_2
  N6: C11.-, LED9.cathode, LED10.cathode, LED11.cathode, LED12.cathode, J9.pin1, R8.Pin_0, U3.Pin_4, VCC3.-
  N7: C11.+, S3.Pin_3, S3.Pin_4, J8.pin1, U3.Pin_8, VCC3.+
  N8: LED9.anode, LED10.anode, LED11.anode, LED12.anode, U3.Pin_5
  N9: S3.Pin_1, S3.Pin_2, R8.Pin_1, U3.Pin_6
  N10: J7.pin1, U3.Pin_2
  N11: C15.-, LED21.cathode, LED27.cathode, LED31.cathode, LED34.cathode, J27.pin1, R11.Pin_0, U9.Pin_4, VCC8.-
  N12: C15.+, S6.Pin_3, S6.Pin_4, J22.pin1, U9.Pin_8, VCC8.+
  N13: C16.-, LED24.cathode, LED25.cathode, LED30.cathode, LED35.cathode, J26.pin1, R14.Pin_0, U8.Pin_4, VCC9.-
  N14: C16.+, S9.Pin_3, S9.Pin_4, J23.pin1, U8.Pin_8, VCC9.+
  N15: LED21.anode, LED27.anode, LED31.anode, LED34.anode, U9.Pin_5
  N16: LED24.anode, LED25.anode, LED30.anode, LED35.anode, U8.Pin_5
  N17: S6.Pin_1, S6.Pin_2, R11.Pin_1, U9.Pin_6
  N18: S9.Pin_1, S9.Pin_2, R14.Pin_1, U8.Pin_6
  N19: J16.pin1, U9.Pin_2
  N20: J18.pin1, U8.Pin_2
  N21: C19.-, LED44.cathode, LED47.cathode, LED49.cathode, LED50.cathode, J39.pin1, R17.Pin_0, U13.Pin_4, VCC12.-
  N22: C19.+, S12.Pin_3, S12.Pin_4, J36.pin1, U13.Pin_8, VCC12.+
  N23: C20.-, LED45.cathode, LED46.cathode, LED48.cathode, LED51.cathode, J38.pin1, R18.Pin_0, U12.Pin_4, VCC13.-
  N24: C20.+, S13.Pin_3, S13.Pin_4, J37.pin1, U12.Pin_8, VCC13.+
  N25: LED44.anode, LED47.anode, LED49.anode, LED50.anode, U13.Pin_5
  N26: LED45.anode, LED46.anode, LED48.anode, LED51.anode, U12.Pin_5
  N27: S12.Pin_1, S12.Pin_2, R17.Pin_1, U13.Pin_6
  N28: S13.Pin_1, S13.Pin_2, R18.Pin_1, U12.Pin_6
  N29: J34.pin1, U13.Pin_2
  N30: J35.pin1, U12.Pin_2
  N31: C21.-, LED52.cathode, LED55.cathode, LED57.cathode, LED58.cathode, J45.pin1, R19.Pin_0, U15.Pin_4, VCC14.-
  N32: C21.+, S14.Pin_3, S14.Pin_4, J42.pin1, U15.Pin_8, VCC14.+
  N33: C22.-, LED53.cathode, LED54.cathode, LED56.cathode, LED59.cathode, J44.pin1, R20.Pin_0, U14.Pin_4, VCC15.-
  N34: C22.+, S15.Pin_3, S15.Pin_4, J43.pin1, U14.Pin_8, VCC15.+
  N35: LED52.anode, LED55.anode, LED57.anode, LED58.anode, U15.Pin_5
  N36: LED53.anode, LED54.anode, LED56.anode, LED59.anode, U14.Pin_5
  N37: S14.Pin_1, S14.Pin_2, R19.Pin_1, U15.Pin_6
  N38: S15.Pin_1, S15.Pin_2, R20.Pin_1, U14.Pin_6
  N39: J40.pin1, U15.Pin_2
  N40: J41.pin1, U14.Pin_2
