# Fritzing sketch Sleep_coach_tiny_schematic_battery (saved by Fritzing 0.7.12b)
breadboards: 1

parts:
  C9 = Electrolytic Capacitor [capacitance=10µF package="100 mil [THT, electrolytic]"]
  LED1 = LED - 5mm [color="Blue (525nm)" package="5 mm [THT]"]
  LED2 = LED - 5mm [color="Blue (525nm)" package="5 mm [THT]"]
  LED4 = LED - 5mm [color="Blue (525nm)" package="5 mm [THT]"]
  S1 = Pushbutton [package="[THT]"]
  J1 = female pin header, 1 pin [form="♀ (female)"]
  J2 = female pin header, 1 pin [form="♀ (female)"]
  J3 = female pin header, 1 pin [form="♀ (female)"]
  U1 = attiny85 [package=dip]
  R6 = Resistor [tolerance=±5% resistance=220 package=THT]
  LED3 = LED - 5mm [color="Blue (525nm)" package="5 mm [THT]"]
  J4 = female pin header, 1 pin [form="♀ (female)"]
  J5 = female pin header, 1 pin [form="♀ (female)"]

nets:
  N1: C9.-, LED1.cathode, LED2.cathode, LED4.cathode, J1.pin1, U1.Pin_4, R6.Pin_0, LED3.cathode, J5.pin1
  N2: C9.+, S1.Pin_3, S1.Pin_4, J2.pin1, U1.Pin_8, J4.pin1
  N3: LED1.anode, LED2.anode, LED4.anode, U1.Pin_5, LED3.anode
  N4: S1.Pin_1, S1.Pin_2, U1.Pin_6, R6.Pin_1
  N5: J3.pin1, U1.Pin_2
