# Fritzing sketch Sleep_coach_tiny_schematic_battery_direct_pot (saved by Fritzing 0.8.5b)
circuit board: 5.08cm x 3.81cm
breadboards: 1

parts:
  C9 = Electrolytic Capacitor [capacitance=10µF package="100 mil [THT, electrolytic]"]
  LED1 = LED - 5mm [color="Blue (525nm)" package="5 mm [THT]"]
  LED2 = LED - 5mm [color="Blue (525nm)" package="5 mm [THT]"]
  LED4 = LED - 5mm [color="Blue (525nm)" package="5 mm [THT]"]
  S1 = Pushbutton [package="[THT]"]
  J1 = female pin header, 1 pin [form="♀ (female)"]  # not connected
  J2 = female pin header, 1 pin [form="♀ (female)"]
  J3 = female pin header, 1 pin [form="♀ (female)"]
  U1 = attiny85 [package=dip]
  R6 = Resistor [tolerance=±5% resistance=220 package=THT]
  LED3 = LED - 5mm [color="Blue (525nm)" package="5 mm [THT]"]
  VCC1 = Battery
  R7 = Resistor [tolerance=±5% resistance=220 package=THT]

nets:
  N1: C9.-, LED1.cathode, LED2.cathode, LED4.cathode, U1.Pin_4, R6.Pin_0, LED3.cathode, VCC1.-
  N2: C9.+, S1.Pin_3, S1.Pin_4, U1.Pin_8, VCC1.+
  N3: LED1.anode, LED2.anode, LED4.anode, LED3.anode, R7.Pin_0
  N4: S1.Pin_1, S1.Pin_2, U1.Pin_6, R6.Pin_1
  N5: J2.pin1, R7.Pin_1
  N6: J3.pin1, U1.Pin_5
